// Logisim project PSG.circ as structural Verilog: 2 circuits, main circuit main
module main (
  input  PSG_CLK,
  input  PSG_TEST_OE,
  input  nPSG_WRITE,
  input  PSG_RESET,
  input  D0,
  input  D1,
  input  D2,
  input  D3,
  input  D4,
  input  D5,
  input  D6,
  input  D7,
  input  D8,
  input  D9,
  input  D10,
  input  D11,
  input  D12,
  input  D13,
  input  D14,
  input  D15,
  input  TEST9,
  input  TEST10,
  input  TEST11,
  output D0_2,
  output D1_2,
  output D2_2,
  output D3_2,
  output D4_2,
  output D5_2,
  output D6_2,
  output D7_2,
  output D8_2,
  output D9_2,
  output D10_2,
  output D11_2,
  output D12_2,
  output D13_2,
  output D14_2,
  output D15_2,
  output DAC0_ATT1,
  output DAC0_ATT2,
  output MUTE_DAC0,
  output [7:0] DAC0,
  output DAC1_ATT1,
  output DAC1_ATT2,
  output MUTE_DAC1,
  output [7:0] DAC1,
  output DAC2_ATT1,
  output DAC2_ATT2,
  output MUTE_DAC2,
  output [7:0] DAC2,
  output DAC3_ATT1,
  output DAC3_ATT2,
  output MUTE_DAC3,
  output [7:0] DAC3
);

  wire _67_out, _80_out, _93_out, _106_out, _111_out, _112_out, _115_out, _118_out, _121_out, _124_out,
       _128_out, _131_out, _134_out, _138_2_out, _138_out, _141_2_out, _141_out, _143_out, _145_out,
       _146_out, _148_2_out, _148_out, _150_out, _151_out, _153_2_out, _153_out, _156_2_out, _156_out,
       _158_out, _159_out, _161_2_out, _161_out, _164_2_out, _164_out, _167_2_out, _167_out, _174_out,
       _175_out, _176_out, _177_out, _222_out, _224_out, _226_out, _228_out, _230_out, _232_out, _234_out,
       _236_out, _238_out, _240_out, _243_out, _246_out, _249_out, _252_out, _254_out, _301_out, _302_out,
       _304_out, _306_out, _308_out, _310_out, _311_out, _313_out, _315_out, _317_out, _319_out, _321_out,
       _323_out, _325_out, _327_out, _329_out, _331_out, _333_out, _350_out, _351_out, _352_out, _358_out,
       _360_out, _365_out, _369_out, _374_out, _380_out, _383_out, _389_out, _390_out, and_1_out, and_2_out,
       and_3_out, and_4_out, and_5_out, and_6_out, and_7_out, and_8_out, and_9_out, and_10_out, and_11_out,
       and_12_out, and_13_out, and_14_out, and_15_out, and_16_out, and_17_out, and_18_out, and_19_out,
       and_20_out, and_21_out, and_22_out, and_23_out, and_24_out, and_25_out, and_26_out, and_27_out,
       and_28_out, and_29_out, and_30_out, and_31_out, and_32_out, and_33_out, and_34_out, and_35_out,
       and_36_out, and_37_out, and_38_out, and_39_out, and_40_out, and_41_out, and_42_out, and_43_out,
       and_44_out, and_45_out, and_46_out, and_47_out, and_48_out, and_49_out, and_50_out, and_51_out,
       and_52_out, and_53_out, and_54_out, and_55_out, and_56_out, and_57_out, and_58_out, and_59_out,
       and_60_out, and_61_out, and_62_out, and_63_out, and_64_out, and_65_out, and_66_out, and_67_out,
       and_68_out, and_69_out, and_70_out, and_71_out, and_72_out, and_73_out, and_74_out, and_75_out,
       and_76_out, and_77_out, and_78_out, and_79_out, and_80_out, and_81_out, and_82_out, and_83_out,
       and_84_out, and_85_out, and_86_out, and_87_out, and_88_out, and_89_out, and_90_out, and_91_out,
       and_92_out, and_93_out, and_94_out, and_95_out, and_96_out, and_97_out, and_98_out, and_99_out,
       and_100_out, and_101_out, and_102_out, and_103_out, and_104_out, and_105_out, and_106_out,
       and_107_out, and_108_out, and_109_out, and_110_out, and_111_out, and_112_out, CLK1, CLK2, CLK3, CLK4,
       clock_1_out, d_ff_1_q, d_ff_2_q, d_ff_3_q, d_ff_4_qn, d_ff_5_qn, d_ff_6_qn, d_ff_7_qn, d_ff_8_qn,
       d_ff_9_q, d_latch_1_q, d_latch_2_q, d_latch_3_q, d_latch_6_q, d_latch_7_q, d_latch_8_q, d_latch_9_q,
       d_latch_10_q, d_latch_11_q, d_latch_12_nq, d_latch_13_nq, d_latch_14_q, d_latch_15_q, d_latch_16_q,
       d_latch_17_q, d_latch_18_q, d_latch_19_q, d_latch_20_q, d_latch_21_q, d_latch_22_q, d_latch_23_q,
       d_latch_24_q, d_latch_25_q, d_latch_26_q, d_latch_27_q, d_latch_28_q, d_latch_29_q, d_latch_30_q,
       d_latch_31_q, d_latch_32_q, d_latch_33_q, d_latch_34_q, d_latch_35_q, d_latch_36_q, d_latch_37_q,
       d_latch_38_q, d_latch_39_q, d_latch_40_q, d_latch_41_q, d_latch_42_q, d_latch_43_q, d_latch_47_nq,
       d_latch_48_nq, d_latch_49_nq, d_latch_50_nq, d_latch_51_nq, d_latch_52_q, d_latch_53_nq,
       d_latch_54_nq, d_latch_55_nq, d_latch_56_nq, d_latch_57_nq, d_latch_58_nq, d_latch_59_nq,
       d_latch_59_q, d_latch_60_nq, d_latch_61_nq, d_latch_62_nq, d_latch_63_nq, d_latch_63_q, d_latch_64_nq,
       d_latch_65_nq, d_latch_66_nq, d_latch_67_nq, d_latch_68_nq, d_latch_69_nq, d_latch_70_nq,
       d_latch_71_nq, d_latch_72_nq, d_latch_73_nq, d_latch_74_nq, d_latch_75_nq, d_latch_76_nq,
       d_latch_77_nq, d_latch_78_nq, d_latch_79_nq, d_latch_80_nq, d_latch_81_nq, d_latch_82_nq,
       d_latch_83_nq, d_latch_84_nq, d_latch_85_nq, d_latch_86_nq, d_latch_87_nq, d_latch_88_nq,
       d_latch_89_nq, d_latch_90_nq, d_latch_91_nq, d_latch_92_nq, d_latch_93_nq, d_latch_94_nq,
       d_latch_95_nq, d_latch_96_nq, d_latch_97_nq, d_latch_98_nq, d_latch_99_nq, d_latch_100_nq,
       d_latch_101_nq, d_latch_102_nq, d_latch_103_nq, d_latch_104_nq, d_latch_105_nq, d_latch_106_nq,
       d_latch_107_nq, d_latch_108_nq, d_latch_109_nq, d_latch_110_nq, d_latch_111_nq, d_latch_112_nq,
       d_latch_113_nq, d_latch_114_nq, d_latch_115_nq, d_latch_116_nq, d_latch_117_nq, d_latch_118_nq,
       d_latch_119_nq, d_latch_120_nq, d_latch_121_nq, d_latch_122_nq, d_latch_123_nq, d_latch_124_nq,
       d_latch_125_nq, d_latch_126_nq, d_latch_127_nq, d_latch_128_nq, d_latch_129_nq, d_latch_130_nq,
       d_latch_131_nq, d_latch_132_nq, d_latch_133_nq, d_latch_134_nq, d_latch_135_nq, d_latch_136_nq,
       d_latch_137_nq, d_latch_138_nq, d_latch_139_nq, d_latch_140_nq, d_latch_141_nq, d_latch_142_nq,
       d_latch_143_nq, d_latch_144_nq, d_latch_145_nq, d_latch_146_nq, d_latch_147_nq, d_latch_148_nq,
       d_latch_149_nq, d_latch_150_nq, d_latch_151_nq, d_latch_152_nq, d_latch_153_nq, d_latch_154_nq,
       d_latch_155_nq, d_latch_156_nq, d_latch_157_nq, d_latch_158_nq, d_latch_159_nq, d_latch_160_nq,
       d_latch_161_nq, d_latch_162_nq, d_latch_163_nq, d_latch_164_nq, d_latch_165_nq, d_latch_166_nq,
       d_latch_167_nq, d_latch_168_nq, d_latch_169_nq, d_latch_170_nq, d_latch_171_nq, d_latch_172_nq,
       d_latch_173_nq, d_latch_174_nq, d_latch_175_nq, d_latch_176_nq, d_latch_177_nq, d_latch_178_nq,
       d_latch_179_nq, d_latch_180_nq, d_latch_181_nq, d_latch_182_nq, d_latch_183_nq, d_latch_184_nq,
       d_latch_185_nq, d_latch_186_nq, d_latch_187_nq, d_latch_188_nq, d_latch_189_q, d_latch_190_q,
       d_latch_191_q, d_latch_192_q, d_latch_193_q, d_latch_194_q, d_latch_195_q, d_latch_196_q,
       d_latch_197_q, d_latch_198_q, d_latch_199_q, d_latch_200_q, d_latch_201_q, d_latch_202_q,
       d_latch_203_q, d_latch_204_q, decoder_1_out0, decoder_1_out1, decoder_1_out2, decoder_1_out3,
       decoder_2_out0, decoder_2_out1, decoder_2_out2, decoder_2_out3, decoder_2_out4, decoder_2_out5,
       decoder_2_out6, decoder_2_out7, decoder_3_out0, decoder_3_out1, decoder_3_out2, decoder_3_out3,
       demultiplexer_1_out0, demultiplexer_1_out1, LATCH0, LATCH1, LATCH2, LATCH3, LATCH4, LATCH4_star,
       LATCH5, LATCH6, LATCH7, LATCH8, LATCH9, LATCH10, multiplexer_1_out, nCLK1, nCLK2, nCLK3, nCLK4,
       nor_1_out, nor_2_out, nor_3_out, nor_4_out, nor_5_out, nor_6_out, nor_7_out, nor_8_out, nor_9_out,
       nor_10_out, nor_11_out, nor_12_out, nor_13_out, nor_14_out, nor_15_out, nor_16_out, nor_17_out,
       nor_18_out, nor_19_out, nor_20_out, not_1_out, not_2_out, not_3_out, not_4_out, not_7_out, not_8_out,
       not_9_out, not_10_out, not_11_out, not_12_out, not_13_out, not_14_out, not_15_out, not_16_out,
       not_17_out, not_18_out, not_19_out, not_20_out, not_21_out, not_22_out, not_23_out, not_24_out,
       not_25_out, not_26_out, not_27_out, not_28_out, not_29_out, not_30_out, not_31_out, not_32_out,
       not_33_out, not_34_out, not_36_out, not_39_out, not_41_out, not_42_out, not_51_out, not_52_out,
       not_53_out, not_54_out, not_56_out, not_57_out, not_58_out, not_59_out, not_60_out, not_63_out,
       not_64_out, not_66_out, not_69_out, not_71_out, not_72_out, not_75_out, not_77_out, not_78_out,
       not_80_out, not_82_out, not_83_out, not_84_out, not_85_out, not_86_out, or_1_out, or_2_out, or_3_out,
       or_4_out, or_5_out, or_6_out, or_7_out, or_8_out, or_9_out, or_10_out, or_11_out, or_12_out,
       or_13_out, or_14_out, or_15_out, or_16_out, or_17_out, or_18_out, or_19_out, or_20_out, or_21_out,
       or_22_out, or_23_out, or_24_out, or_25_out, or_26_out, or_27_out, or_28_out, or_29_out, or_30_out,
       or_31_out, or_32_out, or_33_out, or_34_out, or_35_out, or_36_out, s_r_ff_1_q, s_r_ff_2_q, xor_1_out,
       xor_2_out, xor_3_out, xor_4_out, xor_5_out;
  wire [1:0] d_latch_4_q;
  wire [2:0] _58_out, _71_out, _84_out, _97_out, d_latch_44_q, d_latch_60_q;
  wire [3:0] _125_out, not_46_out;

  Clock clock_1 (.out(clock_1_out));
  not not_1 (not_1_out, clock_1_out);
  not not_2 (not_2_out, not_1_out);
  S_R_Flip_Flop s_r_ff_1 (.S(d_ff_2_q), .R(nPSG_WRITE), .Q(s_r_ff_1_q));  // open: clk, Qn, preset, reset, en
  D_LATCH d_latch_1 (.EN(nPSG_WRITE), .D(D7), .Q(d_latch_1_q));  // open: nQ
  D_LATCH d_latch_2 (.EN(nPSG_WRITE), .D(D6), .Q(d_latch_2_q));  // open: nQ
  D_LATCH d_latch_3 (.EN(LATCH4), .D(_128_out), .Q(d_latch_3_q));  // open: nQ
  D_LATCH d_latch_4 (.EN(LATCH4), .D(_134_out), .Q(d_latch_4_q[0]));  // open: nQ
  D_LATCH d_latch_5 (.EN(LATCH4), .D(_131_out), .Q(d_latch_4_q[1]));  // open: nQ
  D_LATCH d_latch_6 (.EN(nPSG_WRITE), .D(D5), .Q(d_latch_6_q));  // open: nQ
  D_LATCH d_latch_7 (.EN(nPSG_WRITE), .D(D4), .Q(d_latch_7_q));  // open: nQ
  D_LATCH d_latch_8 (.EN(nPSG_WRITE), .D(D3), .Q(d_latch_8_q));  // open: nQ
  D_LATCH d_latch_9 (.EN(nPSG_WRITE), .D(D2), .Q(d_latch_9_q));  // open: nQ
  D_LATCH d_latch_10 (.EN(nPSG_WRITE), .D(D1), .Q(d_latch_10_q));  // open: nQ
  D_LATCH d_latch_11 (.EN(nPSG_WRITE), .D(D0), .Q(d_latch_11_q));  // open: nQ
  nand _354 (CLK1, not_1_out, CLK2);
  nand _354_2 (CLK2, CLK1, not_2_out);
  nor _374 (_374_out, nPSG_WRITE, s_r_ff_1_q);
  not not_3 (not_3_out, d_latch_115_nq);
  and _111 (_111_out, d_latch_1_q, not_3_out);
  and _115 (_115_out, d_latch_2_q, not_3_out);
  and _118 (_118_out, d_latch_6_q, not_3_out);
  and _121 (_121_out, d_latch_7_q, not_3_out);
  not not_4 (not_4_out, not_3_out);
  or _125 (_125_out[0], not_4_out, _124_out);
  and _124 (_124_out, d_latch_8_q, not_3_out);
  or _129 (_125_out[1], not_4_out, _128_out);
  and _128 (_128_out, d_latch_9_q, not_3_out);
  or _132 (_125_out[2], not_4_out, _131_out);
  and _131 (_131_out, d_latch_10_q, not_3_out);
  or _135 (_125_out[3], not_4_out, _134_out);
  and _134 (_134_out, d_latch_11_q, not_3_out);
  not not_5 (nCLK1, CLK1);
  not not_6 (nCLK2, CLK2);
  D_Flip_Flop d_ff_1 (.clk(CLK3), .D(PSG_RESET), .Q(d_ff_1_q));  // open: Qn, preset, en, reset
  D_Flip_Flop d_ff_2 (.clk(CLK1), .D(_374_out), .Q(d_ff_2_q));  // open: Qn, preset, en, reset
  not not_7 (not_7_out, d_ff_1_q);
  not not_8 (not_8_out, not_7_out);
  D_LATCH d_latch_12 (.EN(CLK1), .D(d_ff_2_q), .nQ(d_latch_12_nq));  // open: Q
  and _112 (_112_out, d_ff_2_q, _111_out);
  D_LATCH d_latch_13 (.EN(CLK2), .D(d_latch_12_nq), .nQ(d_latch_13_nq));  // open: Q
  not not_9 (not_9_out, _112_out);
  not not_10 (not_10_out, not_9_out);
  Decoder #(.select(2), .disabled(0), .enable("false")) decoder_1 (
    .out0(decoder_1_out0), .out1(decoder_1_out1), .out2(decoder_1_out2), .out3(decoder_1_out3),
    .sel(d_latch_4_q));
  D_LATCH d_latch_14 (.EN(LATCH5), .D(_118_out), .Q(d_latch_14_q));  // open: nQ
  D_LATCH d_latch_15 (.EN(LATCH6), .D(_118_out), .Q(d_latch_15_q));  // open: nQ
  D_LATCH d_latch_16 (.EN(LATCH7), .D(_118_out), .Q(d_latch_16_q));  // open: nQ
  D_LATCH d_latch_17 (.EN(LATCH5), .D(_121_out), .Q(d_latch_17_q));  // open: nQ
  D_LATCH d_latch_18 (.EN(LATCH6), .D(_121_out), .Q(d_latch_18_q));  // open: nQ
  D_LATCH d_latch_19 (.EN(LATCH7), .D(_121_out), .Q(d_latch_19_q));  // open: nQ
  D_LATCH d_latch_20 (.EN(LATCH5), .D(_124_out), .Q(d_latch_20_q));  // open: nQ
  D_LATCH d_latch_21 (.EN(LATCH6), .D(_124_out), .Q(d_latch_21_q));  // open: nQ
  D_LATCH d_latch_22 (.EN(LATCH7), .D(_124_out), .Q(d_latch_22_q));  // open: nQ
  D_LATCH d_latch_23 (.EN(LATCH5), .D(_128_out), .Q(d_latch_23_q));  // open: nQ
  D_LATCH d_latch_24 (.EN(LATCH6), .D(_128_out), .Q(d_latch_24_q));  // open: nQ
  D_LATCH d_latch_25 (.EN(LATCH7), .D(_128_out), .Q(d_latch_25_q));  // open: nQ
  D_LATCH d_latch_26 (.EN(LATCH5), .D(_131_out), .Q(d_latch_26_q));  // open: nQ
  D_LATCH d_latch_27 (.EN(LATCH6), .D(_131_out), .Q(d_latch_27_q));  // open: nQ
  D_LATCH d_latch_28 (.EN(LATCH7), .D(_131_out), .Q(d_latch_28_q));  // open: nQ
  D_LATCH d_latch_29 (.EN(LATCH5), .D(_134_out), .Q(d_latch_29_q));  // open: nQ
  D_LATCH d_latch_30 (.EN(LATCH6), .D(_134_out), .Q(d_latch_30_q));  // open: nQ
  D_LATCH d_latch_31 (.EN(LATCH7), .D(_134_out), .Q(d_latch_31_q));  // open: nQ
  D_LATCH d_latch_32 (.EN(LATCH8), .D(_124_out), .Q(d_latch_32_q));  // open: nQ
  D_LATCH d_latch_33 (.EN(LATCH9), .D(_124_out), .Q(d_latch_33_q));  // open: nQ
  D_LATCH d_latch_34 (.EN(LATCH10), .D(_124_out), .Q(d_latch_34_q));  // open: nQ
  D_LATCH d_latch_35 (.EN(LATCH8), .D(_128_out), .Q(d_latch_35_q));  // open: nQ
  D_LATCH d_latch_36 (.EN(LATCH9), .D(_128_out), .Q(d_latch_36_q));  // open: nQ
  D_LATCH d_latch_37 (.EN(LATCH10), .D(_128_out), .Q(d_latch_37_q));  // open: nQ
  D_LATCH d_latch_38 (.EN(LATCH8), .D(_131_out), .Q(d_latch_38_q));  // open: nQ
  D_LATCH d_latch_39 (.EN(LATCH9), .D(_131_out), .Q(d_latch_39_q));  // open: nQ
  D_LATCH d_latch_40 (.EN(LATCH10), .D(_131_out), .Q(d_latch_40_q));  // open: nQ
  D_LATCH d_latch_41 (.EN(LATCH8), .D(_134_out), .Q(d_latch_41_q));  // open: nQ
  D_LATCH d_latch_42 (.EN(LATCH9), .D(_134_out), .Q(d_latch_42_q));  // open: nQ
  D_LATCH d_latch_43 (.EN(LATCH10), .D(_134_out), .Q(d_latch_43_q));  // open: nQ
  D_LATCH d_latch_44 (.EN(not_10_out), .D(_115_out), .Q(d_latch_44_q[0]));  // open: nQ
  D_LATCH d_latch_45 (.EN(not_10_out), .D(_118_out), .Q(d_latch_44_q[1]));  // open: nQ
  D_LATCH d_latch_46 (.EN(not_10_out), .D(_121_out), .Q(d_latch_44_q[2]));  // open: nQ
  D_Flip_Flop d_ff_3 (.clk(CLK1), .D(PSG_RESET), .Q(d_ff_3_q));  // open: Qn, preset, en, reset
  and and_1 (and_1_out, 1'b0, not_46_out[0]);
  and and_2 (and_2_out, d_latch_14_q, not_46_out[1]);
  and and_3 (and_3_out, d_latch_15_q, not_46_out[2]);
  and and_4 (and_4_out, d_latch_16_q, not_46_out[3]);
  and and_5 (and_5_out, 1'b0, not_46_out[0]);
  and and_6 (and_6_out, d_latch_17_q, not_46_out[1]);
  and and_7 (and_7_out, d_latch_18_q, not_46_out[2]);
  and and_8 (and_8_out, d_latch_19_q, not_46_out[3]);
  and and_9 (and_9_out, 1'b0, not_46_out[0]);
  and and_10 (and_10_out, d_latch_20_q, not_46_out[1]);
  and and_11 (and_11_out, d_latch_21_q, not_46_out[2]);
  and and_12 (and_12_out, d_latch_22_q, not_46_out[3]);
  and and_13 (and_13_out, decoder_1_out2, not_46_out[0]);
  and and_14 (and_14_out, d_latch_23_q, not_46_out[1]);
  and and_15 (and_15_out, d_latch_24_q, not_46_out[2]);
  and and_16 (and_16_out, d_latch_25_q, not_46_out[3]);
  and and_17 (and_17_out, decoder_1_out1, not_46_out[0]);
  and and_18 (and_18_out, d_latch_26_q, not_46_out[1]);
  and and_19 (and_19_out, d_latch_27_q, not_46_out[2]);
  and and_20 (and_20_out, d_latch_28_q, not_46_out[3]);
  and and_21 (and_21_out, decoder_1_out0, not_46_out[0]);
  and and_22 (and_22_out, d_latch_29_q, not_46_out[1]);
  and and_23 (and_23_out, d_latch_30_q, not_46_out[2]);
  and and_24 (and_24_out, d_latch_31_q, not_46_out[3]);
  and and_25 (and_25_out, 1'b0, not_46_out[0]);
  and and_26 (and_26_out, d_latch_32_q, not_46_out[1]);
  and and_27 (and_27_out, d_latch_33_q, not_46_out[2]);
  and and_28 (and_28_out, d_latch_34_q, not_46_out[3]);
  and and_29 (and_29_out, 1'b0, not_46_out[0]);
  and and_30 (and_30_out, d_latch_35_q, not_46_out[1]);
  and and_31 (and_31_out, d_latch_36_q, not_46_out[2]);
  and and_32 (and_32_out, d_latch_37_q, not_46_out[3]);
  and and_33 (and_33_out, 1'b0, not_46_out[0]);
  and and_34 (and_34_out, d_latch_38_q, not_46_out[1]);
  and and_35 (and_35_out, d_latch_39_q, not_46_out[2]);
  and and_36 (and_36_out, d_latch_40_q, not_46_out[3]);
  and and_37 (and_37_out, 1'b0, not_46_out[0]);
  and and_38 (and_38_out, d_latch_41_q, not_46_out[1]);
  and and_39 (and_39_out, d_latch_42_q, not_46_out[2]);
  and and_40 (and_40_out, d_latch_43_q, not_46_out[3]);
  or _222 (_222_out, and_1_out, and_2_out, and_3_out, and_4_out);
  or _224 (_224_out, and_5_out, and_6_out, and_7_out, and_8_out);
  or _226 (_226_out, and_9_out, and_10_out, and_11_out, and_12_out);
  or _228 (_228_out, and_13_out, and_14_out, and_15_out, and_16_out);
  or _230 (_230_out, and_17_out, and_18_out, and_19_out, and_20_out);
  or _232 (_232_out, and_21_out, and_22_out, and_23_out, and_24_out);
  or _234 (_234_out, and_25_out, and_26_out, and_27_out, and_28_out);
  or _236 (_236_out, and_29_out, and_30_out, and_31_out, and_32_out);
  or _238 (_238_out, and_33_out, and_34_out, and_35_out, and_36_out);
  or _240 (_240_out, and_37_out, and_38_out, and_39_out, and_40_out);
  D_LATCH d_latch_47 (.EN(CLK1), .D(d_ff_3_q), .nQ(d_latch_47_nq));  // open: Q
  D_LATCH d_latch_48 (.EN(CLK4), .D(d_latch_54_nq), .nQ(d_latch_48_nq));  // open: Q
  D_LATCH d_latch_49 (.EN(CLK4), .D(d_latch_55_nq), .nQ(d_latch_49_nq));  // open: Q
  D_LATCH d_latch_50 (.EN(CLK4), .D(d_latch_56_nq), .nQ(d_latch_50_nq));  // open: Q
  D_LATCH d_latch_51 (.EN(CLK4), .D(or_1_out), .nQ(d_latch_51_nq));  // open: Q
  D_LATCH d_latch_52 (.EN(CLK2), .D(d_latch_47_nq), .Q(d_latch_52_q));  // open: nQ
  not not_11 (not_11_out, d_latch_52_q);
  D_LATCH d_latch_53 (.EN(CLK3), .D(d_latch_48_nq), .nQ(d_latch_53_nq));  // open: Q
  D_LATCH d_latch_54 (.EN(CLK3), .D(d_latch_49_nq), .nQ(d_latch_54_nq));  // open: Q
  D_LATCH d_latch_55 (.EN(CLK3), .D(d_latch_50_nq), .nQ(d_latch_55_nq));  // open: Q
  D_LATCH d_latch_56 (.EN(CLK3), .D(d_latch_51_nq), .nQ(d_latch_56_nq));  // open: Q
  nor nor_1 (nor_1_out, _222_out, nor_2_out);
  nor nor_2 (nor_2_out, d_latch_120_nq, or_2_out);
  and and_41 (and_41_out, d_latch_120_nq, or_2_out);
  nor nor_3 (nor_3_out, _224_out, nor_4_out);
  nor nor_4 (nor_4_out, d_latch_124_nq, or_3_out);
  and and_42 (and_42_out, d_latch_124_nq, or_3_out);
  nor nor_5 (nor_5_out, _226_out, nor_6_out);
  nor nor_6 (nor_6_out, d_latch_128_nq, or_4_out);
  and and_43 (and_43_out, d_latch_128_nq, or_4_out);
  nor nor_7 (nor_7_out, _228_out, nor_8_out);
  nor nor_8 (nor_8_out, d_latch_132_nq, or_5_out);
  and and_44 (and_44_out, d_latch_132_nq, or_5_out);
  nor nor_9 (nor_9_out, _230_out, nor_10_out);
  nor nor_10 (nor_10_out, d_latch_136_nq, or_6_out);
  and and_45 (and_45_out, d_latch_136_nq, or_6_out);
  nor nor_11 (nor_11_out, _232_out, nor_12_out);
  nor nor_12 (nor_12_out, d_latch_140_nq, or_7_out);
  and and_46 (and_46_out, d_latch_140_nq, or_7_out);
  nor nor_13 (nor_13_out, _234_out, nor_14_out);
  nor nor_14 (nor_14_out, d_latch_144_nq, or_8_out);
  and and_47 (and_47_out, d_latch_144_nq, or_8_out);
  nor nor_15 (nor_15_out, _236_out, nor_16_out);
  nor nor_16 (nor_16_out, d_latch_148_nq, or_9_out);
  and and_48 (and_48_out, d_latch_148_nq, or_9_out);
  nor nor_17 (nor_17_out, _238_out, nor_18_out);
  nor nor_18 (nor_18_out, d_latch_152_nq, or_10_out);
  and and_49 (and_49_out, d_latch_152_nq, or_10_out);
  nor nor_19 (nor_19_out, _240_out, nor_20_out);
  nor nor_20 (nor_20_out, d_latch_156_nq, 1'b1);
  and and_50 (and_50_out, d_latch_156_nq, 1'b1);
  and _358 (_358_out, not_11_out, d_ff_3_q);
  and _302 (_302_out, d_latch_111_nq, d_latch_53_nq);
  and _304 (_304_out, d_latch_111_nq, d_latch_54_nq);
  and _306 (_306_out, d_latch_111_nq, d_latch_55_nq);
  and _308 (_308_out, d_latch_111_nq, d_latch_56_nq);
  or or_1 (or_1_out, nor_1_out, and_41_out);
  or or_2 (or_2_out, nor_3_out, and_42_out);
  or or_3 (or_3_out, nor_5_out, and_43_out);
  or or_4 (or_4_out, nor_7_out, and_44_out);
  or or_5 (or_5_out, nor_9_out, and_45_out);
  or or_6 (or_6_out, nor_11_out, and_46_out);
  or or_7 (or_7_out, nor_13_out, and_47_out);
  or or_8 (or_8_out, nor_15_out, and_48_out);
  or or_9 (or_9_out, nor_17_out, and_49_out);
  or or_10 (or_10_out, nor_19_out, and_50_out);
  xor xor_1 (xor_1_out, _302_out, d_latch_60_nq);
  xor xor_2 (xor_2_out, _304_out, d_latch_61_nq);
  xor xor_3 (xor_3_out, _306_out, d_latch_62_nq);
  xor xor_4 (xor_4_out, _308_out, d_latch_63_nq);
  nor _301 (_301_out, d_latch_115_nq, or_1_out);
  nor _360 (_360_out, _358_out, d_latch_58_nq);
  xor xor_5 (xor_5_out, d_latch_58_nq, d_latch_59_nq);
  not not_12 (not_12_out, _358_out);
  D_Flip_Flop #(.trigger("high")) d_ff_4 (
    .clk(CLK4), .D(xor_1_out), .Qn(d_ff_4_qn), .en(not_13_out));  // open: Q, preset, reset
  D_Flip_Flop #(.trigger("high")) d_ff_5 (
    .clk(CLK4), .D(xor_2_out), .Qn(d_ff_5_qn), .en(not_13_out));  // open: Q, preset, reset
  D_Flip_Flop #(.trigger("high")) d_ff_6 (
    .clk(CLK4), .D(xor_3_out), .Qn(d_ff_6_qn), .en(not_13_out));  // open: Q, preset, reset
  D_Flip_Flop #(.trigger("high")) d_ff_7 (
    .clk(CLK4), .D(xor_4_out), .Qn(d_ff_7_qn), .en(not_13_out));  // open: Q, preset, reset
  not not_13 (not_13_out, d_latch_115_nq);
  D_LATCH d_latch_57 (.EN(CLK1), .D(_360_out), .nQ(d_latch_57_nq));  // open: Q
  D_Flip_Flop #(.trigger("high")) d_ff_8 (
    .clk(CLK1), .D(xor_5_out), .Qn(d_ff_8_qn), .en(not_12_out));  // open: Q, preset, reset
  and _313 (_313_out, _301_out, d_latch_120_nq);
  and _315 (_315_out, _301_out, d_latch_124_nq);
  and _317 (_317_out, _301_out, d_latch_128_nq);
  and _319 (_319_out, _301_out, d_latch_132_nq);
  and _321 (_321_out, _301_out, d_latch_136_nq);
  and _323 (_323_out, _301_out, d_latch_140_nq);
  and _325 (_325_out, _301_out, d_latch_144_nq);
  and _327 (_327_out, _301_out, d_latch_148_nq);
  and _329 (_329_out, _301_out, d_latch_152_nq);
  and _331 (_331_out, _301_out, d_latch_156_nq);
  D_LATCH d_latch_58 (.EN(CLK2), .D(d_latch_57_nq), .nQ(d_latch_58_nq));  // open: Q
  D_LATCH d_latch_59 (.EN(CLK2), .D(d_ff_8_qn), .Q(d_latch_59_q), .nQ(d_latch_59_nq));
  D_LATCH d_latch_60 (.EN(CLK3), .D(d_ff_4_qn), .Q(d_latch_60_q[0]), .nQ(d_latch_60_nq));
  D_LATCH d_latch_61 (.EN(CLK3), .D(d_ff_5_qn), .Q(d_latch_60_q[1]), .nQ(d_latch_61_nq));
  D_LATCH d_latch_62 (.EN(CLK3), .D(d_ff_6_qn), .Q(d_latch_60_q[2]), .nQ(d_latch_62_nq));
  D_LATCH d_latch_63 (.EN(CLK3), .D(d_ff_7_qn), .Q(d_latch_63_q), .nQ(d_latch_63_nq));
  D_LATCH d_latch_64 (.EN(CLK1), .D(d_latch_59_q), .nQ(d_latch_64_nq));  // open: Q
  not not_14 (not_14_out, _313_out);
  not not_15 (not_15_out, and_56_out);
  not not_16 (not_16_out, _315_out);
  not not_17 (not_17_out, and_59_out);
  not not_18 (not_18_out, _317_out);
  not not_19 (not_19_out, and_62_out);
  not not_20 (not_20_out, _319_out);
  not not_21 (not_21_out, and_65_out);
  not not_22 (not_22_out, _321_out);
  not not_23 (not_23_out, and_68_out);
  not not_24 (not_24_out, _323_out);
  not not_25 (not_25_out, and_71_out);
  not not_26 (not_26_out, _325_out);
  not not_27 (not_27_out, and_74_out);
  not not_28 (not_28_out, _327_out);
  not not_29 (not_29_out, and_77_out);
  not not_30 (not_30_out, _329_out);
  not not_31 (not_31_out, and_80_out);
  not not_32 (not_32_out, _331_out);
  not not_33 (not_33_out, 1'b1);
  not not_34 (not_34_out, d_latch_64_nq);
  Multiplexer #(.disabled(0), .enable("false")) multiplexer_1 (
    .in0(d_latch_60_q[2]), .in1(d_latch_63_q), .out(multiplexer_1_out), .sel(decoder_1_out3));
  and and_51 (and_51_out, not_14_out, and_56_out);
  and and_52 (and_52_out, _313_out, not_15_out);
  and and_53 (and_53_out, _313_out, and_56_out);
  and and_54 (and_54_out, not_16_out, and_59_out);
  and and_55 (and_55_out, _315_out, not_17_out);
  and and_56 (and_56_out, _315_out, and_59_out);
  and and_57 (and_57_out, not_18_out, and_62_out);
  and and_58 (and_58_out, _317_out, not_19_out);
  and and_59 (and_59_out, _317_out, and_62_out);
  and and_60 (and_60_out, not_20_out, and_65_out);
  and and_61 (and_61_out, _319_out, not_21_out);
  and and_62 (and_62_out, _319_out, and_65_out);
  and and_63 (and_63_out, not_22_out, and_68_out);
  and and_64 (and_64_out, _321_out, not_23_out);
  and and_65 (and_65_out, _321_out, and_68_out);
  and and_66 (and_66_out, not_24_out, and_71_out);
  and and_67 (and_67_out, _323_out, not_25_out);
  and and_68 (and_68_out, _323_out, and_71_out);
  and and_69 (and_69_out, not_26_out, and_74_out);
  and and_70 (and_70_out, _325_out, not_27_out);
  and and_71 (and_71_out, _325_out, and_74_out);
  and and_72 (and_72_out, not_28_out, and_77_out);
  and and_73 (and_73_out, _327_out, not_29_out);
  and and_74 (and_74_out, _327_out, and_77_out);
  and and_75 (and_75_out, not_30_out, and_80_out);
  and and_76 (and_76_out, _329_out, not_31_out);
  and and_77 (and_77_out, _329_out, and_80_out);
  and and_78 (and_78_out, not_32_out, 1'b1);
  and and_79 (and_79_out, _331_out, not_33_out);
  and and_80 (and_80_out, _331_out, 1'b1);
  nand _369 (_369_out, d_latch_58_nq, not_34_out);
  nand _365 (_365_out, d_latch_64_nq, d_latch_58_nq);
  or or_11 (or_11_out, and_51_out, and_52_out);
  or or_12 (or_12_out, and_54_out, and_55_out);
  or or_13 (or_13_out, and_57_out, and_58_out);
  or or_14 (or_14_out, and_60_out, and_61_out);
  or or_15 (or_15_out, and_63_out, and_64_out);
  or or_16 (or_16_out, and_66_out, and_67_out);
  or or_17 (or_17_out, and_69_out, and_70_out);
  or or_18 (or_18_out, and_72_out, and_73_out);
  or or_19 (or_19_out, and_75_out, and_76_out);
  or or_20 (or_20_out, and_78_out, and_79_out);
  not not_35 (CLK3, _369_out);
  not not_36 (not_36_out, _369_out);
  not not_37 (nCLK3, not_36_out);
  not not_38 (CLK4, _365_out);
  not not_39 (not_39_out, _365_out);
  not not_40 (nCLK4, not_39_out);
  D_LATCH d_latch_65 (.EN(CLK4), .D(_254_out), .nQ(d_latch_65_nq));  // open: Q
  D_LATCH d_latch_66 (.EN(CLK4), .D(d_latch_111_nq), .nQ(d_latch_66_nq));  // open: Q
  D_LATCH d_latch_67 (.EN(CLK4), .D(d_latch_112_nq), .nQ(d_latch_67_nq));  // open: Q
  D_LATCH d_latch_68 (.EN(CLK4), .D(d_latch_113_nq), .nQ(d_latch_68_nq));  // open: Q
  D_LATCH d_latch_69 (.EN(CLK4), .D(not_8_out), .nQ(d_latch_69_nq));  // open: Q
  D_LATCH d_latch_70 (.EN(CLK4), .D(multiplexer_1_out), .nQ(d_latch_70_nq));  // open: Q
  D_LATCH d_latch_71 (.EN(CLK4), .D(or_11_out), .nQ(d_latch_71_nq));  // open: Q
  D_LATCH d_latch_72 (.EN(CLK4), .D(d_latch_117_nq), .nQ(d_latch_72_nq));  // open: Q
  D_LATCH d_latch_73 (.EN(CLK4), .D(d_latch_118_nq), .nQ(d_latch_73_nq));  // open: Q
  D_LATCH d_latch_74 (.EN(CLK4), .D(d_latch_119_nq), .nQ(d_latch_74_nq));  // open: Q
  D_LATCH d_latch_75 (.EN(CLK4), .D(or_12_out), .nQ(d_latch_75_nq));  // open: Q
  D_LATCH d_latch_76 (.EN(CLK4), .D(d_latch_121_nq), .nQ(d_latch_76_nq));  // open: Q
  D_LATCH d_latch_77 (.EN(CLK4), .D(d_latch_122_nq), .nQ(d_latch_77_nq));  // open: Q
  D_LATCH d_latch_78 (.EN(CLK4), .D(d_latch_123_nq), .nQ(d_latch_78_nq));  // open: Q
  D_LATCH d_latch_79 (.EN(CLK4), .D(or_13_out), .nQ(d_latch_79_nq));  // open: Q
  D_LATCH d_latch_80 (.EN(CLK4), .D(d_latch_125_nq), .nQ(d_latch_80_nq));  // open: Q
  D_LATCH d_latch_81 (.EN(CLK4), .D(d_latch_126_nq), .nQ(d_latch_81_nq));  // open: Q
  D_LATCH d_latch_82 (.EN(CLK4), .D(d_latch_127_nq), .nQ(d_latch_82_nq));  // open: Q
  D_LATCH d_latch_83 (.EN(CLK4), .D(or_14_out), .nQ(d_latch_83_nq));  // open: Q
  D_LATCH d_latch_84 (.EN(CLK4), .D(d_latch_129_nq), .nQ(d_latch_84_nq));  // open: Q
  D_LATCH d_latch_85 (.EN(CLK4), .D(d_latch_130_nq), .nQ(d_latch_85_nq));  // open: Q
  D_LATCH d_latch_86 (.EN(CLK4), .D(d_latch_131_nq), .nQ(d_latch_86_nq));  // open: Q
  D_LATCH d_latch_87 (.EN(CLK4), .D(or_15_out), .nQ(d_latch_87_nq));  // open: Q
  D_LATCH d_latch_88 (.EN(CLK4), .D(d_latch_133_nq), .nQ(d_latch_88_nq));  // open: Q
  D_LATCH d_latch_89 (.EN(CLK4), .D(d_latch_134_nq), .nQ(d_latch_89_nq));  // open: Q
  D_LATCH d_latch_90 (.EN(CLK4), .D(d_latch_135_nq), .nQ(d_latch_90_nq));  // open: Q
  D_LATCH d_latch_91 (.EN(CLK4), .D(or_16_out), .nQ(d_latch_91_nq));  // open: Q
  D_LATCH d_latch_92 (.EN(CLK4), .D(d_latch_137_nq), .nQ(d_latch_92_nq));  // open: Q
  D_LATCH d_latch_93 (.EN(CLK4), .D(d_latch_138_nq), .nQ(d_latch_93_nq));  // open: Q
  D_LATCH d_latch_94 (.EN(CLK4), .D(d_latch_139_nq), .nQ(d_latch_94_nq));  // open: Q
  D_LATCH d_latch_95 (.EN(CLK4), .D(or_17_out), .nQ(d_latch_95_nq));  // open: Q
  D_LATCH d_latch_96 (.EN(CLK4), .D(d_latch_141_nq), .nQ(d_latch_96_nq));  // open: Q
  D_LATCH d_latch_97 (.EN(CLK4), .D(d_latch_142_nq), .nQ(d_latch_97_nq));  // open: Q
  D_LATCH d_latch_98 (.EN(CLK4), .D(d_latch_143_nq), .nQ(d_latch_98_nq));  // open: Q
  D_LATCH d_latch_99 (.EN(CLK4), .D(or_18_out), .nQ(d_latch_99_nq));  // open: Q
  D_LATCH d_latch_100 (.EN(CLK4), .D(d_latch_145_nq), .nQ(d_latch_100_nq));  // open: Q
  D_LATCH d_latch_101 (.EN(CLK4), .D(d_latch_146_nq), .nQ(d_latch_101_nq));  // open: Q
  D_LATCH d_latch_102 (.EN(CLK4), .D(d_latch_147_nq), .nQ(d_latch_102_nq));  // open: Q
  D_LATCH d_latch_103 (.EN(CLK4), .D(or_19_out), .nQ(d_latch_103_nq));  // open: Q
  D_LATCH d_latch_104 (.EN(CLK4), .D(d_latch_149_nq), .nQ(d_latch_104_nq));  // open: Q
  D_LATCH d_latch_105 (.EN(CLK4), .D(d_latch_150_nq), .nQ(d_latch_105_nq));  // open: Q
  D_LATCH d_latch_106 (.EN(CLK4), .D(d_latch_151_nq), .nQ(d_latch_106_nq));  // open: Q
  D_LATCH d_latch_107 (.EN(CLK4), .D(or_20_out), .nQ(d_latch_107_nq));  // open: Q
  D_LATCH d_latch_108 (.EN(CLK4), .D(d_latch_153_nq), .nQ(d_latch_108_nq));  // open: Q
  D_LATCH d_latch_109 (.EN(CLK4), .D(d_latch_154_nq), .nQ(d_latch_109_nq));  // open: Q
  D_LATCH d_latch_110 (.EN(CLK4), .D(d_latch_155_nq), .nQ(d_latch_110_nq));  // open: Q
  D_LATCH d_latch_111 (.EN(CLK3), .D(d_latch_65_nq), .nQ(d_latch_111_nq));  // open: Q
  D_LATCH d_latch_112 (.EN(CLK3), .D(d_latch_66_nq), .nQ(d_latch_112_nq));  // open: Q
  D_LATCH d_latch_113 (.EN(CLK3), .D(d_latch_67_nq), .nQ(d_latch_113_nq));  // open: Q
  D_LATCH d_latch_114 (.EN(CLK3), .D(d_latch_68_nq), .nQ(d_latch_114_nq));  // open: Q
  D_LATCH d_latch_115 (.EN(CLK3), .D(d_latch_69_nq), .nQ(d_latch_115_nq));  // open: Q
  D_LATCH d_latch_116 (.EN(CLK3), .D(d_latch_70_nq), .nQ(d_latch_116_nq));  // open: Q
  D_LATCH d_latch_117 (.EN(CLK3), .D(d_latch_71_nq), .nQ(d_latch_117_nq));  // open: Q
  D_LATCH d_latch_118 (.EN(CLK3), .D(d_latch_72_nq), .nQ(d_latch_118_nq));  // open: Q
  D_LATCH d_latch_119 (.EN(CLK3), .D(d_latch_73_nq), .nQ(d_latch_119_nq));  // open: Q
  D_LATCH d_latch_120 (.EN(CLK3), .D(d_latch_74_nq), .nQ(d_latch_120_nq));  // open: Q
  D_LATCH d_latch_121 (.EN(CLK3), .D(d_latch_75_nq), .nQ(d_latch_121_nq));  // open: Q
  D_LATCH d_latch_122 (.EN(CLK3), .D(d_latch_76_nq), .nQ(d_latch_122_nq));  // open: Q
  D_LATCH d_latch_123 (.EN(CLK3), .D(d_latch_77_nq), .nQ(d_latch_123_nq));  // open: Q
  D_LATCH d_latch_124 (.EN(CLK3), .D(d_latch_78_nq), .nQ(d_latch_124_nq));  // open: Q
  D_LATCH d_latch_125 (.EN(CLK3), .D(d_latch_79_nq), .nQ(d_latch_125_nq));  // open: Q
  D_LATCH d_latch_126 (.EN(CLK3), .D(d_latch_80_nq), .nQ(d_latch_126_nq));  // open: Q
  D_LATCH d_latch_127 (.EN(CLK3), .D(d_latch_81_nq), .nQ(d_latch_127_nq));  // open: Q
  D_LATCH d_latch_128 (.EN(CLK3), .D(d_latch_82_nq), .nQ(d_latch_128_nq));  // open: Q
  D_LATCH d_latch_129 (.EN(CLK3), .D(d_latch_83_nq), .nQ(d_latch_129_nq));  // open: Q
  D_LATCH d_latch_130 (.EN(CLK3), .D(d_latch_84_nq), .nQ(d_latch_130_nq));  // open: Q
  D_LATCH d_latch_131 (.EN(CLK3), .D(d_latch_85_nq), .nQ(d_latch_131_nq));  // open: Q
  D_LATCH d_latch_132 (.EN(CLK3), .D(d_latch_86_nq), .nQ(d_latch_132_nq));  // open: Q
  D_LATCH d_latch_133 (.EN(CLK3), .D(d_latch_87_nq), .nQ(d_latch_133_nq));  // open: Q
  D_LATCH d_latch_134 (.EN(CLK3), .D(d_latch_88_nq), .nQ(d_latch_134_nq));  // open: Q
  D_LATCH d_latch_135 (.EN(CLK3), .D(d_latch_89_nq), .nQ(d_latch_135_nq));  // open: Q
  D_LATCH d_latch_136 (.EN(CLK3), .D(d_latch_90_nq), .nQ(d_latch_136_nq));  // open: Q
  D_LATCH d_latch_137 (.EN(CLK3), .D(d_latch_91_nq), .nQ(d_latch_137_nq));  // open: Q
  D_LATCH d_latch_138 (.EN(CLK3), .D(d_latch_92_nq), .nQ(d_latch_138_nq));  // open: Q
  D_LATCH d_latch_139 (.EN(CLK3), .D(d_latch_93_nq), .nQ(d_latch_139_nq));  // open: Q
  D_LATCH d_latch_140 (.EN(CLK3), .D(d_latch_94_nq), .nQ(d_latch_140_nq));  // open: Q
  D_LATCH d_latch_141 (.EN(CLK3), .D(d_latch_95_nq), .nQ(d_latch_141_nq));  // open: Q
  D_LATCH d_latch_142 (.EN(CLK3), .D(d_latch_96_nq), .nQ(d_latch_142_nq));  // open: Q
  D_LATCH d_latch_143 (.EN(CLK3), .D(d_latch_97_nq), .nQ(d_latch_143_nq));  // open: Q
  D_LATCH d_latch_144 (.EN(CLK3), .D(d_latch_98_nq), .nQ(d_latch_144_nq));  // open: Q
  D_LATCH d_latch_145 (.EN(CLK3), .D(d_latch_99_nq), .nQ(d_latch_145_nq));  // open: Q
  D_LATCH d_latch_146 (.EN(CLK3), .D(d_latch_100_nq), .nQ(d_latch_146_nq));  // open: Q
  D_LATCH d_latch_147 (.EN(CLK3), .D(d_latch_101_nq), .nQ(d_latch_147_nq));  // open: Q
  D_LATCH d_latch_148 (.EN(CLK3), .D(d_latch_102_nq), .nQ(d_latch_148_nq));  // open: Q
  D_LATCH d_latch_149 (.EN(CLK3), .D(d_latch_103_nq), .nQ(d_latch_149_nq));  // open: Q
  D_LATCH d_latch_150 (.EN(CLK3), .D(d_latch_104_nq), .nQ(d_latch_150_nq));  // open: Q
  D_LATCH d_latch_151 (.EN(CLK3), .D(d_latch_105_nq), .nQ(d_latch_151_nq));  // open: Q
  D_LATCH d_latch_152 (.EN(CLK3), .D(d_latch_106_nq), .nQ(d_latch_152_nq));  // open: Q
  D_LATCH d_latch_153 (.EN(CLK3), .D(d_latch_107_nq), .nQ(d_latch_153_nq));  // open: Q
  D_LATCH d_latch_154 (.EN(CLK3), .D(d_latch_108_nq), .nQ(d_latch_154_nq));  // open: Q
  D_LATCH d_latch_155 (.EN(CLK3), .D(d_latch_109_nq), .nQ(d_latch_155_nq));  // open: Q
  D_LATCH d_latch_156 (.EN(CLK3), .D(d_latch_110_nq), .nQ(d_latch_156_nq));  // open: Q
  not not_41 (not_41_out, d_latch_116_nq);
  not not_42 (not_42_out, d_latch_115_nq);
  and _390 (_390_out, multiplexer_1_out, not_41_out);
  nor _254 (_254_out, not_8_out, d_latch_111_nq, d_latch_112_nq, d_latch_113_nq);
  nand _252 (_252_out, d_latch_111_nq, not_42_out);
  nand _249 (_249_out, d_latch_112_nq, not_42_out);
  nand _246 (_246_out, d_latch_113_nq, not_42_out);
  nand _243 (_243_out, d_latch_114_nq, not_42_out);
  Demultiplexer #(.disabled(0), .enable("false")) demultiplexer_1 (
    .out0(demultiplexer_1_out0), .out1(demultiplexer_1_out1), .in(_383_out), .sel(_390_out));
  nand _350 (_350_out, _351_out, _352_out);
  and and_81 (and_81_out, _350_out, demultiplexer_1_out1);
  and and_82 (and_82_out, demultiplexer_1_out0, d_latch_173_nq);
  and and_83 (and_83_out, d_latch_173_nq, demultiplexer_1_out1);
  and and_84 (and_84_out, demultiplexer_1_out0, d_latch_174_nq);
  and and_85 (and_85_out, d_latch_174_nq, demultiplexer_1_out1);
  and and_86 (and_86_out, demultiplexer_1_out0, d_latch_175_nq);
  and and_87 (and_87_out, d_latch_175_nq, demultiplexer_1_out1);
  and and_88 (and_88_out, demultiplexer_1_out0, d_latch_176_nq);
  and and_89 (and_89_out, d_latch_176_nq, demultiplexer_1_out1);
  and and_90 (and_90_out, demultiplexer_1_out0, d_latch_177_nq);
  and and_91 (and_91_out, d_latch_177_nq, demultiplexer_1_out1);
  and and_92 (and_92_out, demultiplexer_1_out0, d_latch_178_nq);
  and and_93 (and_93_out, d_latch_178_nq, demultiplexer_1_out1);
  and and_94 (and_94_out, demultiplexer_1_out0, d_latch_179_nq);
  and and_95 (and_95_out, d_latch_179_nq, demultiplexer_1_out1);
  and and_96 (and_96_out, demultiplexer_1_out0, d_latch_180_nq);
  and and_97 (and_97_out, d_latch_180_nq, demultiplexer_1_out1);
  and and_98 (and_98_out, demultiplexer_1_out0, d_latch_181_nq);
  and and_99 (and_99_out, d_latch_181_nq, demultiplexer_1_out1);
  and and_100 (and_100_out, demultiplexer_1_out0, d_latch_182_nq);
  and and_101 (and_101_out, d_latch_182_nq, demultiplexer_1_out1);
  and and_102 (and_102_out, demultiplexer_1_out0, d_latch_183_nq);
  and and_103 (and_103_out, d_latch_183_nq, demultiplexer_1_out1);
  and and_104 (and_104_out, demultiplexer_1_out0, d_latch_184_nq);
  and and_105 (and_105_out, d_latch_184_nq, demultiplexer_1_out1);
  and and_106 (and_106_out, demultiplexer_1_out0, d_latch_185_nq);
  and and_107 (and_107_out, d_latch_185_nq, demultiplexer_1_out1);
  and and_108 (and_108_out, demultiplexer_1_out0, d_latch_186_nq);
  and and_109 (and_109_out, d_latch_186_nq, demultiplexer_1_out1);
  and and_110 (and_110_out, demultiplexer_1_out0, d_latch_187_nq);
  and and_111 (and_111_out, d_latch_187_nq, demultiplexer_1_out1);
  and and_112 (and_112_out, demultiplexer_1_out0, d_latch_188_nq);
  not not_43 (not_46_out[3], _252_out);
  not not_44 (not_46_out[2], _249_out);
  not not_45 (not_46_out[1], _246_out);
  not not_46 (not_46_out[0], _243_out);
  nand _351 (_351_out, d_latch_3_q, _333_out);
  or or_21 (or_21_out, and_81_out, and_82_out);
  or or_22 (or_22_out, and_83_out, and_84_out);
  or or_23 (or_23_out, and_85_out, and_86_out);
  or or_24 (or_24_out, and_87_out, and_88_out);
  or or_25 (or_25_out, and_89_out, and_90_out);
  or or_26 (or_26_out, and_91_out, and_92_out);
  or or_27 (or_27_out, and_93_out, and_94_out);
  or or_28 (or_28_out, and_95_out, and_96_out);
  or or_29 (or_29_out, and_97_out, and_98_out);
  or or_30 (or_30_out, and_99_out, and_100_out);
  or or_31 (or_31_out, and_101_out, and_102_out);
  or or_32 (or_32_out, and_103_out, and_104_out);
  or or_33 (or_33_out, and_105_out, and_106_out);
  or or_34 (or_34_out, and_107_out, and_108_out);
  or or_35 (or_35_out, and_109_out, and_110_out);
  or or_36 (or_36_out, and_111_out, and_112_out);
  nor _383 (_383_out, not_8_out, d_ff_9_q);
  D_LATCH d_latch_157 (.EN(CLK4), .D(or_21_out), .nQ(d_latch_157_nq));  // open: Q
  D_LATCH d_latch_158 (.EN(CLK4), .D(or_22_out), .nQ(d_latch_158_nq));  // open: Q
  D_LATCH d_latch_159 (.EN(CLK4), .D(or_23_out), .nQ(d_latch_159_nq));  // open: Q
  D_LATCH d_latch_160 (.EN(CLK4), .D(or_24_out), .nQ(d_latch_160_nq));  // open: Q
  D_LATCH d_latch_161 (.EN(CLK4), .D(or_25_out), .nQ(d_latch_161_nq));  // open: Q
  D_LATCH d_latch_162 (.EN(CLK4), .D(or_26_out), .nQ(d_latch_162_nq));  // open: Q
  D_LATCH d_latch_163 (.EN(CLK4), .D(or_27_out), .nQ(d_latch_163_nq));  // open: Q
  D_LATCH d_latch_164 (.EN(CLK4), .D(or_28_out), .nQ(d_latch_164_nq));  // open: Q
  D_LATCH d_latch_165 (.EN(CLK4), .D(or_29_out), .nQ(d_latch_165_nq));  // open: Q
  D_LATCH d_latch_166 (.EN(CLK4), .D(or_30_out), .nQ(d_latch_166_nq));  // open: Q
  D_LATCH d_latch_167 (.EN(CLK4), .D(or_31_out), .nQ(d_latch_167_nq));  // open: Q
  D_LATCH d_latch_168 (.EN(CLK4), .D(or_32_out), .nQ(d_latch_168_nq));  // open: Q
  D_LATCH d_latch_169 (.EN(CLK4), .D(or_33_out), .nQ(d_latch_169_nq));  // open: Q
  D_LATCH d_latch_170 (.EN(CLK4), .D(or_34_out), .nQ(d_latch_170_nq));  // open: Q
  D_LATCH d_latch_171 (.EN(CLK4), .D(or_35_out), .nQ(d_latch_171_nq));  // open: Q
  D_LATCH d_latch_172 (.EN(CLK4), .D(or_36_out), .nQ(d_latch_172_nq));  // open: Q
  D_LATCH d_latch_173 (.EN(CLK3), .D(d_latch_157_nq), .nQ(d_latch_173_nq));  // open: Q
  D_LATCH d_latch_174 (.EN(CLK3), .D(d_latch_158_nq), .nQ(d_latch_174_nq));  // open: Q
  D_LATCH d_latch_175 (.EN(CLK3), .D(d_latch_159_nq), .nQ(d_latch_175_nq));  // open: Q
  D_LATCH d_latch_176 (.EN(CLK3), .D(d_latch_160_nq), .nQ(d_latch_176_nq));  // open: Q
  D_LATCH d_latch_177 (.EN(CLK3), .D(d_latch_161_nq), .nQ(d_latch_177_nq));  // open: Q
  D_LATCH d_latch_178 (.EN(CLK3), .D(d_latch_162_nq), .nQ(d_latch_178_nq));  // open: Q
  D_LATCH d_latch_179 (.EN(CLK3), .D(d_latch_163_nq), .nQ(d_latch_179_nq));  // open: Q
  D_LATCH d_latch_180 (.EN(CLK3), .D(d_latch_164_nq), .nQ(d_latch_180_nq));  // open: Q
  D_LATCH d_latch_181 (.EN(CLK3), .D(d_latch_165_nq), .nQ(d_latch_181_nq));  // open: Q
  D_LATCH d_latch_182 (.EN(CLK3), .D(d_latch_166_nq), .nQ(d_latch_182_nq));  // open: Q
  D_LATCH d_latch_183 (.EN(CLK3), .D(d_latch_167_nq), .nQ(d_latch_183_nq));  // open: Q
  D_LATCH d_latch_184 (.EN(CLK3), .D(d_latch_168_nq), .nQ(d_latch_184_nq));  // open: Q
  D_LATCH d_latch_185 (.EN(CLK3), .D(d_latch_169_nq), .nQ(d_latch_185_nq));  // open: Q
  D_LATCH d_latch_186 (.EN(CLK3), .D(d_latch_170_nq), .nQ(d_latch_186_nq));  // open: Q
  D_LATCH d_latch_187 (.EN(CLK3), .D(d_latch_171_nq), .nQ(d_latch_187_nq));  // open: Q
  D_LATCH d_latch_188 (.EN(CLK3), .D(d_latch_172_nq), .nQ(d_latch_188_nq));  // open: Q
  S_R_Flip_Flop s_r_ff_2 (.S(LATCH4_star), .R(d_ff_9_q), .Q(s_r_ff_2_q));  // open: clk, Qn, preset, reset, en
  nand _352 (_352_out, _380_out, _389_out, _310_out, _311_out);
  xor _333 (_333_out, d_latch_185_nq, d_latch_188_nq);
  nor _311 (_311_out, d_latch_173_nq, d_latch_174_nq, d_latch_175_nq, d_latch_176_nq);
  nor _310 (_310_out, d_latch_177_nq, d_latch_178_nq, d_latch_179_nq);
  nor _389 (_389_out, d_latch_180_nq, d_latch_181_nq, d_latch_182_nq, d_latch_183_nq);
  nor _380 (_380_out, d_latch_184_nq, d_latch_185_nq, d_latch_186_nq, d_latch_187_nq);
  D_Flip_Flop d_ff_9 (.clk(CLK4), .D(s_r_ff_2_q), .Q(d_ff_9_q));  // open: Qn, preset, en, reset
  Decoder #(.select(3), .disabled(0), .enable("false")) decoder_2 (
    .out0(decoder_2_out0), .out1(decoder_2_out1), .out2(decoder_2_out2), .out3(decoder_2_out3),
    .out4(decoder_2_out4), .out5(decoder_2_out5), .out6(decoder_2_out6), .out7(decoder_2_out7),
    .sel(d_latch_44_q));
  D_LATCH d_latch_189 (.EN(LATCH0), .D(_125_out[0]), .Q(d_latch_189_q));  // open: nQ
  D_LATCH d_latch_190 (.EN(LATCH0), .D(_125_out[1]), .Q(d_latch_190_q));  // open: nQ
  D_LATCH d_latch_191 (.EN(LATCH0), .D(_125_out[2]), .Q(d_latch_191_q));  // open: nQ
  D_LATCH d_latch_192 (.EN(LATCH0), .D(_125_out[3]), .Q(d_latch_192_q));  // open: nQ
  D_LATCH d_latch_193 (.EN(LATCH1), .D(_125_out[0]), .Q(d_latch_193_q));  // open: nQ
  D_LATCH d_latch_194 (.EN(LATCH1), .D(_125_out[1]), .Q(d_latch_194_q));  // open: nQ
  D_LATCH d_latch_195 (.EN(LATCH1), .D(_125_out[2]), .Q(d_latch_195_q));  // open: nQ
  D_LATCH d_latch_196 (.EN(LATCH1), .D(_125_out[3]), .Q(d_latch_196_q));  // open: nQ
  D_LATCH d_latch_197 (.EN(LATCH2), .D(_125_out[0]), .Q(d_latch_197_q));  // open: nQ
  D_LATCH d_latch_198 (.EN(LATCH2), .D(_125_out[1]), .Q(d_latch_198_q));  // open: nQ
  D_LATCH d_latch_199 (.EN(LATCH2), .D(_125_out[2]), .Q(d_latch_199_q));  // open: nQ
  D_LATCH d_latch_200 (.EN(LATCH2), .D(_125_out[3]), .Q(d_latch_200_q));  // open: nQ
  D_LATCH d_latch_201 (.EN(LATCH3), .D(_125_out[0]), .Q(d_latch_201_q));  // open: nQ
  D_LATCH d_latch_202 (.EN(LATCH3), .D(_125_out[1]), .Q(d_latch_202_q));  // open: nQ
  D_LATCH d_latch_203 (.EN(LATCH3), .D(_125_out[2]), .Q(d_latch_203_q));  // open: nQ
  D_LATCH d_latch_204 (.EN(LATCH3), .D(_125_out[3]), .Q(d_latch_204_q));  // open: nQ
  nor _174 (_174_out, d_latch_60_q[0], TEST9);
  nor _175 (_175_out, d_latch_60_q[1], TEST9);
  nor _176 (_176_out, d_latch_60_q[2], TEST9);
  nor _177 (_177_out, d_latch_187_nq, TEST9);
  Decoder #(.select(2), .disabled(0)) decoder_3 (
    .out0(decoder_3_out0), .out1(decoder_3_out1), .out2(decoder_3_out2), .out3(decoder_3_out3),
    .sel({TEST11, TEST10}), .en(TEST9));
  and _138 (_138_out, decoder_2_out4, d_latch_13_nq);
  and _141 (_141_out, decoder_2_out5, d_latch_13_nq);
  and _156 (_156_out, decoder_2_out6, d_latch_13_nq);
  and _164 (_164_out, decoder_2_out7, d_latch_13_nq);
  and _167 (_167_out, decoder_2_out3, d_latch_13_nq);
  and _148 (_148_out, decoder_2_out2, d_latch_13_nq);
  and _153 (_153_out, decoder_2_out1, d_latch_13_nq);
  and _161 (_161_out, decoder_2_out0, d_latch_13_nq);
  or _58 (_58_out[0], d_latch_189_q, _174_out);
  or _61 (_58_out[1], d_latch_190_q, _174_out);
  or _64 (_58_out[2], d_latch_191_q, _174_out);
  or _67 (_67_out, d_latch_192_q, _174_out);
  or _71 (_71_out[0], d_latch_193_q, _175_out);
  or _74 (_71_out[1], d_latch_194_q, _175_out);
  or _77 (_71_out[2], d_latch_195_q, _175_out);
  or _80 (_80_out, d_latch_196_q, _175_out);
  or _84 (_84_out[0], d_latch_197_q, _176_out);
  or _87 (_84_out[1], d_latch_198_q, _176_out);
  or _90 (_84_out[2], d_latch_199_q, _176_out);
  or _93 (_93_out, d_latch_200_q, _176_out);
  or _97 (_97_out[0], d_latch_201_q, _177_out);
  or _100 (_97_out[1], d_latch_202_q, _177_out);
  or _103 (_97_out[2], d_latch_203_q, _177_out);
  or _106 (_106_out, d_latch_204_q, _177_out);
  not not_47 (MUTE_DAC0, decoder_3_out0);
  not not_48 (MUTE_DAC1, decoder_3_out1);
  not not_49 (MUTE_DAC2, decoder_3_out2);
  not not_50 (MUTE_DAC3, decoder_3_out3);
  nor _138_2 (_138_2_out, _138_out, not_8_out);
  not not_51 (not_51_out, _138_2_out);
  nor _141_2 (_141_2_out, _141_out, not_8_out);
  not not_52 (not_52_out, _141_2_out);
  not not_53 (not_53_out, _156_2_out);
  nor _156_2 (_156_2_out, _156_out, not_8_out);
  not not_54 (not_54_out, _164_2_out);
  nor _164_2 (_164_2_out, _164_out, not_8_out);
  nor _167_2 (_167_2_out, _167_out, not_8_out);
  not not_55 (LATCH4_star, _167_2_out);
  nor _148_2 (_148_2_out, _148_out, not_8_out);
  not not_56 (not_56_out, _148_2_out);
  nor _153_2 (_153_2_out, _153_out, not_8_out);
  not not_57 (not_57_out, _153_2_out);
  nor _161_2 (_161_2_out, _161_out, not_8_out);
  not not_58 (not_58_out, _161_2_out);
  or _143 (_143_out, not_8_out, _111_out);
  not not_59 (not_59_out, _111_out);
  and _145 (_145_out, not_59_out, not_56_out);
  and _146 (_146_out, _143_out, not_56_out);
  and _150 (_150_out, not_59_out, not_57_out);
  and _151 (_151_out, _143_out, not_57_out);
  and _158 (_158_out, not_59_out, not_58_out);
  and _159 (_159_out, _143_out, not_58_out);
  not not_60 (not_60_out, not_51_out);
  not not_61 (LATCH0, not_60_out);
  not not_62 (LATCH1, not_63_out);
  not not_63 (not_63_out, not_52_out);
  not not_64 (not_64_out, not_53_out);
  not not_65 (LATCH2, not_64_out);
  not not_66 (not_66_out, not_54_out);
  not not_67 (LATCH3, not_66_out);
  not not_68 (LATCH4, not_69_out);
  not not_69 (not_69_out, LATCH4_star);
  not not_70 (LATCH5, not_71_out);
  not not_71 (not_71_out, _145_out);
  not not_72 (not_72_out, _146_out);
  not not_73 (LATCH8, not_72_out);
  not not_74 (LATCH6, not_75_out);
  not not_75 (not_75_out, _150_out);
  not not_76 (LATCH9, not_77_out);
  not not_77 (not_77_out, _151_out);
  not not_78 (not_78_out, _158_out);
  not not_79 (LATCH7, not_78_out);
  not not_80 (not_80_out, _159_out);
  not not_81 (LATCH10, not_80_out);
  not not_82 (not_82_out, MUTE_DAC0);
  not not_83 (not_83_out, MUTE_DAC1);
  not not_84 (not_84_out, MUTE_DAC2);
  not not_85 (not_85_out, MUTE_DAC3);
  not not_86 (not_86_out, PSG_TEST_OE);
  assign D0_2 = not_86_out ? ~_58_out[0] : 1'bz;  // Controlled_Inverter controlled_inverter_1
  assign D1_2 = not_86_out ? ~_58_out[1] : 1'bz;  // Controlled_Inverter controlled_inverter_2
  assign D2_2 = not_86_out ? ~_58_out[2] : 1'bz;  // Controlled_Inverter controlled_inverter_3
  assign D3_2 = not_86_out ? ~_67_out : 1'bz;  // Controlled_Inverter controlled_inverter_4
  assign D4_2 = not_86_out ? ~_71_out[0] : 1'bz;  // Controlled_Inverter controlled_inverter_5
  assign D5_2 = not_86_out ? ~_71_out[1] : 1'bz;  // Controlled_Inverter controlled_inverter_6
  assign D6_2 = not_86_out ? ~_71_out[2] : 1'bz;  // Controlled_Inverter controlled_inverter_7
  assign D7_2 = not_86_out ? ~_80_out : 1'bz;  // Controlled_Inverter controlled_inverter_8
  assign D8_2 = not_86_out ? ~_84_out[0] : 1'bz;  // Controlled_Inverter controlled_inverter_9
  assign D9_2 = not_86_out ? ~_84_out[1] : 1'bz;  // Controlled_Inverter controlled_inverter_10
  assign D10_2 = not_86_out ? ~_84_out[2] : 1'bz;  // Controlled_Inverter controlled_inverter_11
  assign D11_2 = not_86_out ? ~_93_out : 1'bz;  // Controlled_Inverter controlled_inverter_12
  assign D12_2 = not_86_out ? ~_97_out[0] : 1'bz;  // Controlled_Inverter controlled_inverter_13
  assign D13_2 = not_86_out ? ~_97_out[1] : 1'bz;  // Controlled_Inverter controlled_inverter_14
  assign D14_2 = not_86_out ? ~_97_out[2] : 1'bz;  // Controlled_Inverter controlled_inverter_15
  assign D15_2 = not_86_out ? ~_106_out : 1'bz;  // Controlled_Inverter controlled_inverter_16
  nand _3 (DAC0_ATT1, _106_out, not_82_out);
  nand _2 (DAC0_ATT2, DAC0_ATT1, not_82_out);
  Decoder #(.select(3), .disabled(0), .enable("false")) decoder_4 (
    .out0(DAC0[0]), .out1(DAC0[1]), .out2(DAC0[2]), .out3(DAC0[3]), .out4(DAC0[4]), .out5(DAC0[5]),
    .out6(DAC0[6]), .out7(DAC0[7]), .sel(_97_out));
  nand _17 (DAC1_ATT1, _93_out, not_83_out);
  nand _16 (DAC1_ATT2, DAC1_ATT1, not_83_out);
  Decoder #(.select(3), .disabled(0), .enable("false")) decoder_5 (
    .out0(DAC1[0]), .out1(DAC1[1]), .out2(DAC1[2]), .out3(DAC1[3]), .out4(DAC1[4]), .out5(DAC1[5]),
    .out6(DAC1[6]), .out7(DAC1[7]), .sel(_84_out));
  nand _31 (DAC2_ATT1, _80_out, not_84_out);
  nand _30 (DAC2_ATT2, DAC2_ATT1, not_84_out);
  Decoder #(.select(3), .disabled(0), .enable("false")) decoder_6 (
    .out0(DAC2[0]), .out1(DAC2[1]), .out2(DAC2[2]), .out3(DAC2[3]), .out4(DAC2[4]), .out5(DAC2[5]),
    .out6(DAC2[6]), .out7(DAC2[7]), .sel(_71_out));
  nand _45 (DAC3_ATT1, _67_out, not_85_out);
  nand _44 (DAC3_ATT2, DAC3_ATT1, not_85_out);
  Decoder #(.select(3), .disabled(0), .enable("false")) decoder_7 (
    .out0(DAC3[0]), .out1(DAC3[1]), .out2(DAC3[2]), .out3(DAC3[3]), .out4(DAC3[4]), .out5(DAC3[5]),
    .out6(DAC3[6]), .out7(DAC3[7]), .sel(_58_out));

  // Other names for the same wires on the sheet: nPSG_WR = nPSG_WRITE

  // Notes on the sheet:
  //   353
  //   354
  //   373
  //   110
  //   114
  //   220
  //   218
  //   219
  //   117
  //   120
  //   123
  //   127
  //   130
  //   133
  //   312
  //   126
  //   354
  //   354
  //   377
  //   378
  //   375
  //   379
  //   113
  //   169 - 170
  //   214 - 217
  //   complementary clock
  //   complementary clock
  //   LATCH11
  //   376
  //   116
  //   119
  //   122
  //   178
  //   179
  //   180
  //   181
  //   182
  //   183
  //   184
  //   185
  //   186
  //   187
  //   188
  //   189
  //   190
  //   191
  //   192
  //   193
  //   194
  //   195
  //   199
  //   200
  //   201
  //   202
  //   203
  //   204
  //   205
  //   206
  //   207
  //   208
  //   209
  //   210
  //   355
  //   357
  //   356
  //   257
  //   258
  //   259
  //   260
  //   223
  //   225
  //   227
  //   229
  //   231
  //   233
  //   235
  //   237
  //   239
  //   241
  //   /EN
  //   /EN
  //   c1
  //   c2
  //   303
  //   305
  //   307
  //   309
  //   CLOCK DIVIDER
  //   361
  //   362
  //   a
  //   b
  //   a
  //   b
  //   a
  //   b
  //   a
  //   b
  //   a
  //   b
  //   a
  //   b
  //   a
  //   b
  //   a
  //   b
  //   a
  //   b
  //   a
  //   b
  //   363
  //   INVERTED LATCH
  //   !!!
  //   314
  //   316
  //   318
  //   320
  //   322
  //   324
  //   326
  //   328
  //   330
  //   332
  //   364
  //   393
  //   394
  //   C
  //   Not used
  //   C
  //   C
  //   C
  //   C
  //   C
  //   C
  //   C
  //   C
  //   C
  //   S
  //   S
  //   S
  //   S
  //   S
  //   S
  //   S
  //   S
  //   S
  //   S
  //   372
  //   371
  //   370
  //   366
  //   368
  //   367
  //   C2
  //   C1
  //   253
  //   250
  //   247
  //   244
  //   256
  //   392
  //   264
  //   263
  //   262
  //   261
  //   268
  //   267
  //   266
  //   265
  //   272
  //   271
  //   270
  //   269
  //   276
  //   275
  //   274
  //   273
  //   280
  //   279
  //   278
  //   277
  //   284
  //   283
  //   282
  //   281
  //   288
  //   287
  //   286
  //   285
  //   292
  //   291
  //   290
  //   289
  //   296
  //   295
  //   294
  //   293
  //   300
  //   299
  //   298
  //   297
  //   complementary clock
  //   complementary clock
  //   391
  //   255
  //   384-388
  //   CLK1
  //   CLK2
  //   CLK3
  //   CLK4
  //   251
  //   248
  //   245
  //   242
  //   349
  //   348
  //   347
  //   346
  //   345
  //   344
  //   343
  //   342
  //   341
  //   340
  //   339
  //   338
  //   337
  //   336
  //   335
  //   334
  //   381
  //   382
  //   RNDOUT
  //   139,142,149,154
  //   157,162,163,166
  //   171-173
  //   TEST9
  //   4
  //   5
  //   6
  //   7
  //   3
  //   2
  //   1
  //   0
  //   59
  //   62
  //   65
  //   68
  //   72
  //   75
  //   78
  //   81
  //   85
  //   88
  //   91
  //   94
  //   98
  //   101
  //   104
  //   107
  //   395 - 404
  //   137
  //   140
  //   155
  //   165
  //   168
  //   147
  //   152
  //   160
  //   144
  //   69
  //   95
  //   108
  //   221
  //   196
  //   211
  //   197
  //   212
  //   198
  //   213
  //   82
  //   102
  //   105
  //   1
  //   4-14
  //   15
  //   18-28
  //   29
  //   32-42
  //   43
  //   46-56
  //   57
  //   60
  //   63
  //   66
  //   70
  //   73
  //   76
  //   79
  //   83
  //   86
  //   89
  //   92
  //   96
  //   99
endmodule

module D_LATCH (
  input  EN,
  input  D,
  output Q,
  output nQ
);

  D_Flip_Flop #(.trigger("high")) d_ff_1 (.clk(EN), .D(D), .Q(Q), .Qn(nQ));  // open: preset, en, reset
endmodule
