// Logisim project cell18.circ as structural Verilog: 1 circuit, main circuit main
module main (
  input  nc1,
  input  nc2,
  input  a,
  input  c1,
  input  c2,
  input  r,
  input  nc1_2,
  input  nc2_2,
  input  r_2,
  input  a_2,
  input  c1_2,
  input  c2_2,
  output c,
  output s,
  output s_2,
  output c_2
);

  wire and_1_out, not_1_out, not_2_out, not_3_out, not_5_out, transistor_1_out, transistor_3_out,
       transistor_7_out, transistor_8_out, transistor_10_out, transistor_14_out, transistor_15_out,
       transistor_16_out, transistor_18_out, transistor_19_out, transistor_20_out, transistor_22_out,
       transistor_23_out, transistor_25_out, transistor_29_out, transistor_30_out, transistor_32_out,
       transistor_33_out, transistor_34_out, transistor_36_out, xor_1_out;

  Transistor transistor_1 (.in(1'b1), .out(transistor_1_out), .gate(a));
  Transistor #(.\type ("n")) transistor_2 (.in(1'b0), .out(transistor_1_out), .gate(a));
  Transistor transistor_3 (.in(1'b1), .out(transistor_3_out), .gate(transistor_23_out));
  Transistor transistor_4 (.in(transistor_3_out), .out(c), .gate(transistor_1_out));
  Transistor #(.\type ("n")) transistor_5 (.in(1'b0), .out(c), .gate(transistor_23_out));
  Transistor #(.\type ("n")) transistor_6 (.in(1'b0), .out(c), .gate(transistor_1_out));
  Transistor transistor_7 (.in(1'b1), .out(transistor_7_out), .gate(transistor_1_out));
  Transistor #(.\type ("n")) transistor_8 (.in(1'b0), .out(transistor_8_out), .gate(r));
  Transistor transistor_9 (.in(1'b1), .out(transistor_7_out), .gate(transistor_23_out));
  Transistor transistor_10 (.in(transistor_7_out), .out(transistor_10_out), .gate(r));
  Transistor transistor_11 (.in(transistor_10_out), .out(transistor_8_out), .gate(c));
  Transistor #(.\type ("n")) transistor_12 (.in(1'b0), .out(transistor_8_out), .gate(c));
  Transistor #(.\type ("n")) transistor_13 (.in(transistor_14_out), .out(transistor_8_out), .gate(transistor_23_out));
  Transistor #(.\type ("n")) transistor_14 (.in(1'b0), .out(transistor_14_out), .gate(transistor_1_out));
  Transistor transistor_15 (.in(1'b1), .out(transistor_15_out), .gate(transistor_8_out));
  Transistor transistor_16 (.in(transistor_15_out), .out(transistor_16_out), .gate(nc1));
  Transistor #(.\type ("n")) transistor_17 (.in(transistor_18_out), .out(transistor_16_out), .gate(c1));
  Transistor #(.\type ("n")) transistor_18 (.in(1'b0), .out(transistor_18_out), .gate(transistor_8_out));
  not not_1 (not_1_out, a_2);
  Transistor transistor_19 (.in(1'b1), .out(transistor_19_out), .gate(transistor_16_out));
  Transistor transistor_20 (.in(transistor_19_out), .out(transistor_20_out), .gate(nc2));
  Transistor #(.\type ("n")) transistor_21 (.in(transistor_22_out), .out(transistor_20_out), .gate(c2));
  Transistor #(.\type ("n")) transistor_22 (.in(1'b0), .out(transistor_22_out), .gate(transistor_16_out));
  Transistor transistor_23 (.in(1'b1), .out(transistor_23_out), .gate(transistor_20_out));
  Transistor #(.\type ("n")) transistor_24 (.in(1'b0), .out(transistor_23_out), .gate(transistor_20_out));
  not not_2 (not_2_out, r_2);
  Transistor transistor_25 (.in(1'b1), .out(transistor_25_out), .gate(transistor_20_out));
  Transistor #(.\type ("n")) transistor_26 (.in(1'b0), .out(transistor_25_out), .gate(transistor_20_out));
  xor xor_1 (xor_1_out, not_5_out, not_1_out);
  Transistor transistor_27 (.in(1'b1), .out(s), .gate(transistor_25_out));
  Transistor #(.\type ("n")) transistor_28 (.in(1'b0), .out(s), .gate(transistor_25_out));
  and and_1 (and_1_out, not_2_out, xor_1_out);
  Transistor transistor_29 (.in(1'b1), .out(transistor_29_out), .gate(and_1_out));
  Transistor transistor_30 (.in(transistor_29_out), .out(transistor_30_out), .gate(nc1_2));
  Transistor #(.\type ("n")) transistor_31 (.in(transistor_32_out), .out(transistor_30_out), .gate(c1_2));
  Transistor #(.\type ("n")) transistor_32 (.in(1'b0), .out(transistor_32_out), .gate(and_1_out));
  nor nor_1 (c_2, not_5_out, not_1_out);
  Transistor transistor_33 (.in(1'b1), .out(transistor_33_out), .gate(transistor_30_out));
  Transistor transistor_34 (.in(transistor_33_out), .out(transistor_34_out), .gate(nc2_2));
  Transistor #(.\type ("n")) transistor_35 (.in(transistor_36_out), .out(transistor_34_out), .gate(c2_2));
  Transistor #(.\type ("n")) transistor_36 (.in(1'b0), .out(transistor_36_out), .gate(transistor_30_out));
  not not_3 (not_3_out, transistor_34_out);
  not not_4 (s_2, not_3_out);
  not not_5 (not_5_out, transistor_34_out);
endmodule
